// Logisim project RS_Latches.circ as structural Verilog
module RS_Latches (
  input  S,
  input  CLK,
  input  R,
  input  S_2,
  input  CLK_2,
  input  R_2,
  output Q,
  output nQ,
  output Q_2,
  output nQ_2
);

  wire and_1_out, and_2_out, nand_1_out, nand_2_out;

  nand nand_1 (nand_1_out, S, CLK);
  nand nand_2 (nand_2_out, CLK, R);
  and and_1 (and_1_out, R_2, CLK_2);
  and and_2 (and_2_out, CLK_2, S_2);
  nand nand_3 (Q, nand_1_out, nQ);
  nand nand_4 (nQ, Q, nand_2_out);
  nor nor_1 (Q_2, and_1_out, nQ_2);
  nor nor_2 (nQ_2, Q_2, and_2_out);

  // Other names for the same wires on the sheet: R_t = R_2; S_t = S_2
endmodule
